// Logisim project ex01.circ as structural Verilog: 1 circuit, main circuit main
module main (
  input  SEL,
  input  X,
  input  Y,
  output out_4
);

  wire and_1_out, and_2_out, not_1_out;

  not not_1 (not_1_out, SEL);
  and and_1 (and_1_out, SEL, X);
  and and_2 (and_2_out, not_1_out, Y);
  or or_1 (out_4, and_1_out, and_2_out);

  // Notes on the sheet:
  //   . 
endmodule
