// Logisim project ex02.circ as structural Verilog: 1 circuit, main circuit main
module main (
  input  SEL,
  output A,
  output B
);

  wire not_1_out;

  not not_1 (not_1_out, SEL);
  and and_1 (A, 1'b1, SEL);
  and and_2 (B, not_1_out, 1'b1);
endmodule
